// Logisim project FalconPipeline.circ as structural Verilog: 8 circuits, main circuit main
module main (
  input  RST
);

  wire ALUsource, ALUzero, and_1_out, Branch, CLK, FLUSH, FLUSHD, Jump, JumpR, MemRead, MemReadR, MemToReg,
       MemToRegR, MemWrite, MemWriteR, or_1_out, RegWrite, RegWriteP, Store;
  wire [2:0] ALUoperation, funct, ImmSel, rd, rdP, rs1, rs2;
  wire [3:0] opcode;
  wire [5:0] ImediatoB, ImediatoI, ImediatoS;
  wire [7:0] adder_3_out, ALUdata, data, dataR, Imediato, ImediatoR, MemData, nextPC, PC, pc_2, pc_2R,
       PCbranch, rd1, rd1R, rd2, rdstore, rdstoreR, RegData;
  wire [8:0] ImediatoJ, TipoR;
  wire [15:0] instrucao, instrucaoF, instrucaoR;

  Clock u_CLK (.out(CLK));
  Adder adder_1 (.a(PC), .b(Imediato), .out(PCbranch));  // open: cin, cout
  Adder adder_2 (.a(PC), .b(8'h2), .out(pc_2));  // open: cin, cout
  // Probe on PC
  InstructionFetch instructionfetch_1 (.clk(CLK), .rst(RST), .nextPC(nextPC), .pcAtual(PC), .instrucao(instrucao));
  Register #(.width(16)) u_instrucao (.D(instrucao), .en(1'b1), .clk(CLK), .Q(instrucaoR), .clr(RST));
  Register u_pc_2 (.D(pc_2), .en(1'b1), .clk(CLK), .Q(pc_2R), .clr(RST));
  Register register_1 (.D(Imediato), .en(1'b1), .clk(CLK), .Q(ImediatoR), .clr(RST));
  Multiplexer #(.width(16)) multiplexer_1 (.in0(instrucaoR), .in1({16{1'b0}}), .out(instrucaoF), .sel(FLUSHD));
  Register register_2 (.D(rd1), .en(1'b1), .clk(CLK), .Q(rd1R), .clr(RST));
  InstructionDecode instructiondecode_1 (
    .Instrucao(instrucaoF), .funct(funct), .rs2(rs2), .rs1(rs1), .rd(rd), .opcode(opcode),
    .ImediatoTipoI(ImediatoI), .ImediatoTipoS(ImediatoS), .ImediatoTipoB(ImediatoB),
    .ImediatoTipoJ(ImediatoJ), .TipoR(TipoR));
  Register #(.width(1)) register_3 (.D(MemWrite), .en(1'b1), .clk(CLK), .Q(MemWriteR), .clr(RST));
  Adder adder_3 (.a(ImediatoR), .b(rd1R), .out(adder_3_out));  // open: cin, cout
  ImmGen immgen_1 (
    .ImmSel(ImmSel), .ImmI(ImediatoI), .ImmS(ImediatoS), .ImmB(ImediatoB), .ImmJ(ImediatoJ),
    .Imediato(Imediato));
  and and_1 (and_1_out, ALUzero, Branch);
  or or_1 (or_1_out, and_1_out, Jump);
  Register #(.width(1)) register_4 (.D(MemRead), .en(1'b1), .clk(CLK), .Q(MemReadR), .clr(RST));
  Multiplexer #(.width(8)) multiplexer_2 (.in0(pc_2), .in1(PCbranch), .out(nextPC), .sel(or_1_out));
  UC uc_1 (
    .tipoR(TipoR), .opcode(opcode), .funct(funct), .ResultBranch(data), .clk(CLK), .ImmSel(ImmSel),
    .ALUOp(ALUoperation), .ALUSource(ALUsource), .Branch(Branch), .MemRead(MemRead), .MemToReg(MemToReg),
    .MemWrite(MemWrite), .RegWrite(RegWrite), .Jump(Jump), .Store(Store), .Flush(FLUSH));  // open: PCSource
  Register register_5 (.D(rdstore), .en(1'b1), .clk(CLK), .Q(rdstoreR), .clr(RST));
  DM dm_1 (
    .Adress(adder_3_out), .WriteEnable(MemWriteR), .MemRead(MemReadR), .Clock(CLK), .WriteData(rdstoreR),
    .ReadData(MemData));
  Multiplexer #(.width(8)) multiplexer_3 (.in0(dataR), .in1(MemData), .out(RegData), .sel(MemToRegR));
  Registers registers_1 (
    .clk(CLK), .rst(RST), .regwrite(RegWriteP), .rdRead(rd), .rdWrite(rdP), .rs2(rs2), .rs1(rs1),
    .data(RegData), .PC2(pc_2), .Jump(JumpR), .readdata1(rd1), .readdata2(rd2), .rdstore(rdstore));
  Register #(.width(1)) register_6 (.D(MemToReg), .en(1'b1), .clk(CLK), .Q(MemToRegR), .clr(RST));
  Register #(.width(1)) register_7 (.D(RegWrite), .en(1'b1), .clk(CLK), .Q(RegWriteP), .clr(RST));
  Multiplexer #(.width(8)) multiplexer_4 (.in0(rd2), .in1(Imediato), .out(ALUdata), .sel(ALUsource));
  ALU alu_1 (
    .src1(rd1), .src2(ALUdata), .rd(rdstore), .ALUOperation(ALUoperation), .opcode(opcode), .result(data),
    .ALUzero(ALUzero));
  Register register_8 (.D(data), .en(1'b1), .clk(CLK), .Q(dataR), .clr(RST));
  Register #(.width(3)) register_9 (.D(rd), .en(1'b1), .clk(CLK), .Q(rdP), .clr(RST));
  Register #(.width(1)) register_10 (.D(FLUSH), .en(1'b1), .clk(CLK), .Q(FLUSHD), .clr(RST));
  Register #(.width(1)) register_11 (.D(Jump), .en(1'b1), .clk(CLK), .Q(JumpR), .clr(RST));

  // Notes on the sheet:
  //   1
  //   3
  //   2
endmodule

module InstructionFetch (
  input  clk,
  input  rst,
  input  [7:0] nextPC,
  output [7:0] pcAtual,
  output [15:0] instrucao
);

  Register RegistradorPC (.D(nextPC), .en(1'b1), .clk(clk), .Q(pcAtual), .clr(rst));
  // ROM #(.line("dual")) ROM1: pin names not known; wires that end beside it: pcAtual, instrucao[15:8], instrucao[7:0]

  // Other names for the same wires on the sheet: nPC[7:0] = nextPC

  // Notes on the sheet:
  //   contents of ROM1 (hex, n*v repeats v):
  //   0 0 12 10 24 40 26 41 28 42 2a 43 c a4 4c a d 5c 4c 4 1c 2 3c 50 3c 51 40 32 1c 1 3c 50 3c 51 40 2e
  //   30 50 30 51 40 2b
endmodule

module InstructionDecode (
  input  [15:0] Instrucao,
  output [2:0] funct,
  output [2:0] rs2,
  output [2:0] rs1,
  output [2:0] rd,
  output [3:0] opcode,
  output [5:0] ImediatoTipoI,
  output [5:0] ImediatoTipoS,
  output [5:0] ImediatoTipoB,
  output [8:0] ImediatoTipoJ,
  output [8:0] TipoR
);


  assign funct = Instrucao[2:0];
  assign ImediatoTipoB = Instrucao[5:0];
  assign ImediatoTipoI = Instrucao[5:0];
  assign ImediatoTipoJ = Instrucao[8:0];
  assign ImediatoTipoS = Instrucao[5:0];
  assign opcode = Instrucao[15:12];
  assign rd = Instrucao[11:9];
  assign rs1 = Instrucao[8:6];
  assign rs2 = Instrucao[5:3];
  assign TipoR = Instrucao[11:3];

  // Other names for the same wires on the sheet: imediatoB[5:0] = Instrucao[5:0]; imediatoI[5:0] = Instrucao[5:0];
  //   imediatoJ[8:0] = Instrucao[8:0]; imediatoS[5:0] = Instrucao[5:0]

  // Notes on the sheet:
  //   Imediato Tipo I
  //   Imediato Tipo B
  //   Imediato Tipo S
  //   Imediato Tipo J
endmodule

module Registers (
  input  clk,
  input  rst,
  input  regwrite,
  input  [2:0] rdRead,
  input  [2:0] rdWrite,
  input  [2:0] rs2,
  input  [2:0] rs1,
  input  [7:0] data,
  input  [7:0] PC2,
  input  Jump,
  output [7:0] readdata1,
  output [7:0] readdata2,
  output [7:0] rdstore
);

  wire wera, wes0, wes1, wet0, wet1, wet2, wet3;
  wire [7:0] dataFinal, qra, qs0, qs1, qt0, qt1, qt2, qt3, qzero;

  Demultiplexer #(.select(3)) demultiplexer_1 (
    .out1(wet0), .out2(wet1), .out3(wet2), .out4(wet3), .out5(wes0), .out6(wes1), .out7(wera), .in(regwrite),
    .sel(rdWrite));  // open: out0
  Register #(.trigger("falling")) zero (.D({8{1'b0}}), .clk(clk), .Q(qzero), .clr(rst));  // open: en
  Register #(.trigger("falling")) t3 (.D(dataFinal), .en(wet3), .clk(clk), .Q(qt3), .clr(rst));
  Register #(.trigger("falling")) t0 (.D(dataFinal), .en(wet0), .clk(clk), .Q(qt0), .clr(rst));
  Register #(.trigger("falling")) s0 (.D(dataFinal), .en(wes0), .clk(clk), .Q(qs0), .clr(rst));
  Multiplexer #(.width(8)) multiplexer_1 (.in0(data), .in1(PC2), .out(dataFinal), .sel(Jump));
  Register #(.trigger("falling")) t1 (.D(dataFinal), .en(wet1), .clk(clk), .Q(qt1), .clr(rst));
  Register #(.trigger("falling")) s1 (.D(dataFinal), .en(wes1), .clk(clk), .Q(qs1), .clr(rst));
  Register #(.trigger("falling")) t2 (.D(dataFinal), .en(wet2), .clk(clk), .Q(qt2), .clr(rst));
  Register #(.trigger("falling")) ra (.D(dataFinal), .en(wera), .clk(clk), .Q(qra), .clr(rst));
  Multiplexer #(.select(3), .width(8)) multiplexer_2 (
    .in0(qzero), .in1(qt0), .in2(qt1), .in3(qt2), .in4(qt3), .in5(qs0), .in6(qs1), .in7(qra), .out(rdstore),
    .sel(rdRead));
  Multiplexer #(.select(3), .width(8)) multiplexer_3 (
    .in0(qzero), .in1(qt0), .in2(qt1), .in3(qt2), .in4(qt3), .in5(qs0), .in6(qs1), .in7(qra),
    .out(readdata1), .sel(rs1));
  Multiplexer #(.select(3), .width(8)) multiplexer_4 (
    .in0(qzero), .in1(qt0), .in2(qt1), .in3(qt2), .in4(qt3), .in5(qs0), .in6(qs1), .in7(qra),
    .out(readdata2), .sel(rs2));

  // Other names for the same wires on the sheet: pc_2[7:0] = PC2; rd1[7:0] = readdata1; rd2[7:0] = readdata2;
  //   rdR[2:0] = rdRead; rdW[2:0] = rdWrite; rw = regwrite
endmodule

module ALU (
  input  [7:0] src1,
  input  [7:0] src2,
  input  [7:0] rd,
  input  [2:0] ALUOperation,
  input  [3:0] opcode,
  output [7:0] result,
  output ALUzero
);

  wire comparator_1_eq, comparator_1_lt, comparator_2_lt, comparator_3_eq, comparator_4_eq, not_1_out;
  wire [7:0] add, andd, beq, blt, bne, orr, result_t, resultI, shiftaritmeticright, shiftlogicright, SLLI,
       slt, subb, xorr;

  Adder adder_1 (.a(src1), .b(src2), .out(add));  // open: cin, cout
  Subtractor subtractor_1 (.a(src1), .b(src2), .out(subb));  // open: bin, bout
  assign xorr = src1 ^ src2;  // XOR_Gate xor_1, 8 bits wide
  assign orr = src1 | src2;  // OR_Gate or_1, 8 bits wide
  assign andd = src1 & src2;  // AND_Gate and_1, 8 bits wide
  Comparator #(.mode("unsigned")) comparator_1 (
    .a(rd), .b(src1), .eq(comparator_1_eq), .lt(comparator_1_lt));  // open: gt
  assign beq = {{7{1'b0}}, comparator_1_eq};  // Bit_Extender bit_extender_1
  assign blt = {{7{1'b0}}, comparator_1_lt};  // Bit_Extender bit_extender_2
  Shifter shifter_1 (.in(src1), .\dist (src2[2:0]), .out(resultI));
  Shifter #(.shift("lr")) shifter_2 (.in(src1), .\dist (src2[2:0]), .out(shiftlogicright));
  Shifter #(.shift("ar")) shifter_3 (.in(src1), .\dist (src2[2:0]), .out(shiftaritmeticright));
  Comparator comparator_2 (.a(src1), .b(src2), .lt(comparator_2_lt));  // open: gt, eq
  Comparator comparator_3 (.a(rd), .b(src1), .eq(comparator_3_eq));  // open: gt, lt
  assign slt = {{7{1'b0}}, comparator_2_lt};  // Bit_Extender bit_extender_3
  not not_1 (not_1_out, comparator_3_eq);
  Shifter shifter_4 (.in(src1), .\dist (src2[2:0]), .out(SLLI));
  assign bne = {{7{1'b0}}, not_1_out};  // Bit_Extender bit_extender_4
  Multiplexer #(.select(3), .width(8)) multiplexer_1 (
    .in0(add), .in1(subb), .in2(andd), .in3(orr), .in4(slt), .in5(resultI), .in6(shiftlogicright),
    .out(result_t), .sel(ALUOperation));  // open: in7
  Multiplexer #(.select(4), .width(8)) multiplexer_2 (
    .in0(result_t), .in1(result_t), .in2(result_t), .in3(result_t), .in4(beq), .in5(bne), .in6(result_t),
    .in7(resultI), .in8(blt), .in9(result_t), .in10(result_t), .in11(result_t), .in12(result_t),
    .in13(result_t), .in14(resultI), .in15(result_t), .out(result), .sel(opcode));
  Comparator comparator_4 (.a({8{1'b0}}), .b(result), .eq(comparator_4_eq));  // open: gt, lt
  not not_2 (ALUzero, comparator_4_eq);

  // Other names for the same wires on the sheet: realresult[7:0] = result; rs1B[7:0] = rd;
  //   shiftlogicleft[7:0] = resultI; sltu[7:0] = blt; zero = ALUzero

  // Notes on the sheet:
  //   OPCODES
endmodule

module ImmGen (
  input  [2:0] ImmSel,
  input  [5:0] ImmI,
  input  [5:0] ImmS,
  input  [5:0] ImmB,
  input  [8:0] ImmJ,
  output [7:0] Imediato
);

  wire [7:0] b_16b, i_16b, j_16b, s_16b;

  assign i_16b = {{2{ImmI[5]}}, ImmI};  // Bit_Extender bit_extender_1
  assign s_16b = {{2{ImmS[5]}}, ImmS};  // Bit_Extender bit_extender_2
  assign b_16b = {{1{ImmB[5]}}, {ImmB, 1'b0}};  // Bit_Extender bit_extender_3
  Bit_Extender #(.in_width(10), .out_width(8)) bit_extender_4 (.in({ImmJ, 1'b0}), .out(j_16b));
  Multiplexer #(.select(3), .width(8)) multiplexer_1 (
    .in0(i_16b), .in1(s_16b), .in2(b_16b), .in3(j_16b), .out(Imediato), .sel(ImmSel));  // open: in4, in5, in6, in7

  // Other names for the same wires on the sheet: Imm[7:0] = Imediato

  // Notes on the sheet:
  //   Instrucao Tipo I
  //   Instrucao Tipo S
  //   Instrucao Tipo B
  //   Instrucao Tipo J
endmodule

module UC (
  input  [8:0] tipoR,
  input  [3:0] opcode,
  input  [2:0] funct,
  input  [7:0] ResultBranch,
  input  clk,
  output [2:0] ImmSel,
  output [2:0] ALUOp,
  output ALUSource,
  output Branch,
  output MemRead,
  output MemToReg,
  output MemWrite,
  output RegWrite,
  output PCSource,
  output Jump,
  output Store,
  output Flush
);

  wire and_1_out, and_2_out, comparator_1_eq, comparator_2_gt, ImediatoI, not_1_out, tipoBBEQ, tipoBBLT,
       tipoBBNE, tipoIAritmetico, tipoIShift, tipoR_t;

  or TipoI (ImediatoI, tipoIAritmetico, MemRead, tipoIShift);
  or TipoB (Branch, tipoBBEQ, tipoBBNE, tipoBBLT);
  Decoder #(.select(4)) decoder_1 (
    .out0(tipoR_t), .out1(tipoIAritmetico), .out2(MemRead), .out3(MemWrite), .out4(tipoBBEQ),
    .out5(tipoBBNE), .out6(Jump), .out7(tipoIShift), .out8(tipoBBLT), .sel(opcode), .en(1'b1));  // open: out9, out10, out11, out12, out13, out14, out15
  or or_1 (ImmSel[1], Branch, Jump);
  Comparator #(.width(9)) comparator_1 (.a(tipoR), .b({9{1'b0}}), .eq(comparator_1_eq));  // open: gt, lt
  or or_2 (ImmSel[0], MemWrite, Jump);
  not not_1 (not_1_out, comparator_1_eq);
  and and_1 (and_1_out, not_1_out, tipoR_t);
  and and_2 (and_2_out, Branch, ResultBranch[0]);
  Comparator #(.mode("unsigned"), .width(1)) comparator_2 (
    .a(tipoR_t), .b(1'b0), .gt(comparator_2_gt));  // open: eq, lt
  or or_3 (RegWrite, and_1_out, ImediatoI, Jump);
  or or_4 (Flush, and_2_out, Jump);
  Multiplexer #(.width(3)) multiplexer_1 (.in0(3'b000), .in1(funct), .out(ALUOp), .sel(comparator_2_gt));
  or or_5 (ALUSource, MemWrite, ImediatoI);
  or or_6 (PCSource, Branch, Jump);

  assign ImmSel[2] = 1'b0;
  assign MemToReg = MemRead;
  assign Store = MemWrite;

  // Other names for the same wires on the sheet: ImediatoB = Branch; ImmR[8:0] = tipoR; tipoILoad = MemRead;
  //   tipoJ = Jump; tipoS = MemWrite
endmodule

module DM (
  input  [7:0] Adress,
  input  WriteEnable,
  input  MemRead,
  input  Clock,
  input  [7:0] WriteData,
  output [7:0] ReadData
);

  wire [7:0] ram_1_dout;

  RAM #(.asyncread("true"), .trigger("falling")) ram_1 (
    .addr(Adress), .we(WriteEnable), .oe(MemRead), .clk(Clock), .din(WriteData), .dout(ram_1_dout));
  assign ReadData = MemRead ? ram_1_dout : 8'bz;  // Controlled_Buffer controlled_buffer_1

  // Other names for the same wires on the sheet: CLK = Clock; StoreData[7:0] = WriteData
endmodule
